// Logisim project ex-two-bit-seq.circ as structural Verilog: 1 circuit, main circuit main
module main (
  input  Clock,
  input  Reset
);

  wire and_1_out, and_2_out, d_ff_1_q, d_ff_2_q, not_1_out, or_1_out;

  D_Flip_Flop d_ff_1 (.clk(Clock), .D(not_1_out), .Q(d_ff_1_q), .reset(Reset));  // open: Qn, preset, en
  D_Flip_Flop d_ff_2 (.clk(Clock), .D(or_1_out), .Q(d_ff_2_q), .reset(Reset));  // open: Qn, preset, en
  // Probe on d_ff_1_q
  // Probe on d_ff_2_q
  not not_1 (not_1_out, d_ff_1_q);
  and and_1 (and_1_out, ~d_ff_1_q, d_ff_2_q);  // AND_Gate
  and and_2 (and_2_out, d_ff_1_q, ~d_ff_2_q);  // AND_Gate
  or or_1 (or_1_out, and_1_out, and_2_out);

  // Notes on the sheet:
  //   Q_1
  //   Q_0
  //   Q_1
  //   Q_0
endmodule
