// Logisim project proj-template.circ as structural Verilog: 1 circuit, main circuit main
module main (
  input  Clock,
  input  Reset
);

  wire undriven, undriven_2, undriven_3, undriven_4;
  wire [3:0] d_ff_4_q;

  D_Flip_Flop d_ff_1 (.clk(Clock), .D(undriven_4), .Q(d_ff_4_q[3]), .reset(Reset));  // open: Qn, preset, en
  D_Flip_Flop d_ff_2 (.clk(Clock), .D(undriven_3), .Q(d_ff_4_q[2]), .reset(Reset));  // open: Qn, preset, en
  D_Flip_Flop d_ff_3 (.clk(Clock), .D(undriven_2), .Q(d_ff_4_q[1]), .reset(Reset));  // open: Qn, preset, en
  D_Flip_Flop d_ff_4 (.clk(Clock), .D(undriven), .Q(d_ff_4_q[0]), .reset(Reset));  // open: Qn, preset, en
  // Probe on d_ff_4_q[3]
  // Probe on d_ff_4_q[2]
  // Probe on d_ff_4_q[1]
  // Probe on d_ff_4_q[0]
  Hex_Digit_Display hex_digit_display_1 (.value(d_ff_4_q));  // open: dp
  // Probe on undriven_4
  // Probe on undriven_3
  // Probe on undriven_2
  // Probe on undriven

  // Notes on the sheet:
  //   Q3
  //   Q2
  //   Q1
  //   Q0
  //   Q3
  //   Q2
  //   Q1
  //   Q0
  //   Q3'
  //   Q2'
  //   Q1'
  //   Q0'
endmodule
