// Logisim project D-flip-flop-rising.circ as structural Verilog: 1 circuit, main circuit main
module main (
  input  Clock,
  input  Data,
  output Q___output
);

  D_Flip_Flop d_ff_1 (.clk(Clock), .D(Data), .Q(Q___output));  // open: Qn, preset, en, reset

  // Notes on the sheet:
  //   D Flip Flop
  //   Rising Edge
endmodule
