// Logisim project candy-state-2.circ as structural Verilog: 1 circuit, main circuit main
module main (
  input  Clock,
  input  Reset,
  input  I,
  output Q_0,
  output Q_1,
  output O_0,
  output O_1,
  output Q_prime__0,
  output Q_prime__1,
  output O_prime__0,
  output O_prime__1
);

  wire and_2_out, and_3_out, and_4_out, and_5_out, not_1_out, not_2_out, not_3_out, not_4_out, not_5_out,
       not_6_out, not_7_out, not_8_out;

  D_Flip_Flop d_ff_1 (.clk(Clock), .D(Q_prime__0), .Q(Q_0), .reset(Reset));  // open: Qn, preset, en
  D_Flip_Flop d_ff_2 (.clk(Clock), .D(Q_prime__1), .Q(Q_1), .reset(Reset));  // open: Qn, preset, en
  D_Flip_Flop d_ff_3 (.clk(Clock), .D(O_prime__0), .Q(O_0), .reset(Reset));  // open: Qn, preset, en
  D_Flip_Flop d_ff_4 (.clk(Clock), .D(O_prime__1), .Q(O_1), .reset(Reset));  // open: Qn, preset, en
  not not_1 (not_1_out, Q_1);
  not not_2 (not_2_out, Q_1);
  not not_3 (not_3_out, Q_0);
  not not_4 (not_4_out, Q_1);
  not not_5 (not_5_out, I);
  not not_6 (not_6_out, Q_0);
  not not_7 (not_7_out, Q_1);
  not not_8 (not_8_out, I);
  and and_1 (O_prime__0, Q_0, not_1_out, I);
  and and_2 (and_2_out, Q_0, not_2_out);
  and and_3 (and_3_out, I, Q_1);
  and and_4 (and_4_out, not_3_out, not_4_out, I);
  and and_5 (and_5_out, Q_1, not_5_out);
  and and_6 (Q_prime__1, not_6_out, not_7_out, not_8_out);
  or or_1 (O_prime__1, and_2_out, and_3_out);
  or or_2 (Q_prime__0, and_4_out, and_5_out);

  // Notes on the sheet:
  //   Current State Storage
  //   Input
  //   Next State Logic
  //   Output State Storage
  //   change
  //   Current States
  //   Q_0
  //   Q_1
  //   I
  //   candy
  //   Next States
  //   change
  //   candy
  //   Next Output State
  //   O'_0
  //   O'_1
  //   Q'_0
  //   Q'_1
endmodule
