// Logisim project d-flip-flop-falling.circ as structural Verilog: 1 circuit, main circuit main
module main (
  input  Clock,
  input  Data
);

  wire and_1_out, and_2_out, and_3_out, and_4_out, nor_1_out, nor_2_out, nor_3_out, nor_4_out, not_1_out,
       not_2_out, not_3_out;

  not not_1 (not_1_out, Data);
  and and_1 (and_1_out, Clock, not_1_out);
  and and_2 (and_2_out, Clock, Data);
  nor nor_1 (nor_1_out, and_1_out, nor_2_out);
  nor nor_2 (nor_2_out, nor_1_out, and_2_out);
  not not_2 (not_2_out, Clock);
  not not_3 (not_3_out, nor_1_out);
  and and_3 (and_3_out, not_2_out, not_3_out);
  and and_4 (and_4_out, not_2_out, nor_1_out);
  nor nor_3 (nor_3_out, and_3_out, nor_4_out);
  nor nor_4 (nor_4_out, nor_3_out, and_4_out);
  // Probe on nor_3_out
  // Probe on nor_4_out

  // Notes on the sheet:
  //   D Latch 1
  //   D Flip Flop
  //   Falling Edge
  //   D Latch 2
  //   Q - output
  //   !Q - output
  //   inverted
endmodule
