// Logisim project d-latch.circ as structural Verilog: 1 circuit, main circuit main
module main (
  input  Clock,
  input  Data
);

  wire and_1_out, and_2_out, nor_1_out, nor_2_out, not_1_out;

  not not_1 (not_1_out, Data);
  and and_1 (and_1_out, Clock, not_1_out);
  and and_2 (and_2_out, Clock, Data);
  nor nor_1 (nor_1_out, and_1_out, nor_2_out);
  nor nor_2 (nor_2_out, nor_1_out, and_2_out);
  // Probe on nor_1_out
  // Probe on nor_2_out

  // Notes on the sheet:
  //   D Latch
  //   Reset
  //   Set
  //   S-R Latch
  //   Q - output
  //   !Q - output
  //   inverted
endmodule
