// Logisim project s-r-latch.circ as structural Verilog: 1 circuit, main circuit main
module main (
  input  Reset,
  input  Set
);

  wire nor_1_out, nor_2_out;

  nor nor_1 (nor_1_out, Reset, nor_2_out);
  nor nor_2 (nor_2_out, nor_1_out, Set);
  // Probe on nor_1_out
  // Probe on nor_2_out

  // Notes on the sheet:
  //   S-R Latch
  //   Q - output
  //   !Q - output
  //   inverted
endmodule
