// Logisim project seq-flip-flot.circ as structural Verilog: 1 circuit, main circuit main
module main (
  input  Reset
);

  wire clock_1_out, d_ff_1_q, d_ff_2_q, not_1_out, not_2_out;

  Clock clock_1 (.out(clock_1_out));
  // Probe on not_1_out
  D_Flip_Flop d_ff_1 (.clk(clock_1_out), .D(not_1_out), .Q(d_ff_1_q), .reset(Reset));  // open: Qn, preset, en
  not not_1 (not_1_out, d_ff_2_q);
  not not_2 (not_2_out, clock_1_out);
  // Probe on d_ff_2_q
  D_Flip_Flop d_ff_2 (.clk(not_2_out), .D(d_ff_1_q), .Q(d_ff_2_q), .reset(Reset));  // open: Qn, preset, en

  // Notes on the sheet:
  //   Clock
  //   Data Input
  //   Flip-Flop-1
  //   Flip-Flop-2
  //   Data Output
endmodule
